// Logisim project 4-1_mux.circ as structural Verilog: 2 circuits, main circuit main
module main (
  input  In0,
  input  In1,
  input  In2,
  input  In3,
  input  sel0,
  input  sel1,
  output Out
);

  wire n2_1_mux_1_out, n2_1_mux_2_out;

  _2_1_mux u_2_1_mux_1 (.In0(In0), .In1(In1), .sel(sel0), .out(n2_1_mux_1_out));
  _2_1_mux u_2_1_mux_2 (.In0(In2), .In1(In3), .sel(sel0), .out(n2_1_mux_2_out));
  _2_1_mux u_2_1_mux_3 (.In0(n2_1_mux_1_out), .In1(n2_1_mux_2_out), .sel(sel1), .out(Out));
endmodule

module _2_1_mux (
  input  In0,
  input  In1,
  input  sel,
  output out
);

  wire and_1_out, and_2_out, not_1_out;

  not not_1 (not_1_out, sel);
  and and_1 (and_1_out, In0, In0, not_1_out);
  and and_2 (and_2_out, In1, sel);
  or or_1 (out, and_1_out, and_2_out);
endmodule
