// Logisim project 4Adder.circ as structural Verilog: 1 circuit, main circuit main
module main (
  input  A1,
  input  B1,
  input  A2,
  input  B2,
  input  A3,
  input  B3,
  input  A4,
  input  B4,
  output Sum1,
  output Sum2,
  output Sum3,
  output Sum4,
  output Cout
);

  wire main_1_cout, main_2_cout, main_3_cout;

  _1FAdder_main main_1 (.A(A1), .B(B1), .Cin(1'b0), .Sum(Sum1), .Cout(main_1_cout));
  _1FAdder_main main_2 (.A(A2), .B(B2), .Cin(main_1_cout), .Sum(Sum2), .Cout(main_2_cout));
  _1FAdder_main main_3 (.A(A3), .B(B3), .Cin(main_2_cout), .Sum(Sum3), .Cout(main_3_cout));
  _1FAdder_main main_4 (.A(A4), .B(B4), .Cin(main_3_cout), .Sum(Sum4), .Cout(Cout));
endmodule
