// Logisim project 4bit-Adder.circ as structural Verilog: 2 circuits, main circuit main
module main (
  input  [3:0] A,
  input  [3:0] B,
  output Carry_out,
  output Sum3,
  output Sum2,
  output Sum1,
  output Sum0
);

  wire fadder_2_cout, fadder_3_cout, fadder_4_cout;

  FAdder fadder_1 (.A(A[3]), .B(B[3]), .Cin(fadder_2_cout), .Sum(Sum3), .Cout(Carry_out));
  FAdder fadder_2 (.A(A[2]), .B(B[2]), .Cin(fadder_3_cout), .Sum(Sum2), .Cout(fadder_2_cout));
  FAdder fadder_3 (.A(A[1]), .B(B[1]), .Cin(fadder_4_cout), .Sum(Sum1), .Cout(fadder_3_cout));
  FAdder fadder_4 (.A(A[0]), .B(B[0]), .Cin(1'b0), .Sum(Sum0), .Cout(fadder_4_cout));

  // Notes on the sheet:
  //   1비트 FA이용한 4 비트 덧셈기
endmodule

module FAdder (
  input  A,
  input  B,
  input  Cin,
  output Sum,
  output Cout
);

  wire A_B_out, A_Cin_out, B_Cin_out, xor_1_out;

  xor xor_1 (xor_1_out, A, B);
  and A_B (A_B_out, A, B);
  and B_Cin (B_Cin_out, Cin, B);
  and A_Cin (A_Cin_out, A, Cin);
  xor xor_2 (Sum, xor_1_out, Cin);
  or or_1 (Cout, A_B_out, B_Cin_out, A_Cin_out);

  // Notes on the sheet:
  //   1 비트 덧셈기 (가산기)
endmodule
