// Logisim project ALU_Design.circ as structural Verilog: 1 circuit, main circuit main
module main (
  input  [3:0] A,
  input  [3:0] B,
  input  [2:0] F,
  output [3:0] out_4
);

  wire [3:0] A_B_out, adder_1_out, AorB_out, bit_extender_1_out, multiplexer_1_out, not_1_out;

  assign not_1_out = ~B;  // NOT_Gate not_1, 4 bits wide
  Multiplexer #(.width(4)) multiplexer_1 (.in0(B), .in1(not_1_out), .out(multiplexer_1_out), .sel(F[2]));  // open: en
  assign A_B_out = A & multiplexer_1_out;  // AND_Gate A_B, 4 bits wide
  assign AorB_out = A | multiplexer_1_out;  // OR_Gate AorB, 4 bits wide
  Adder #(.width(4)) adder_1 (.a(A), .b(multiplexer_1_out), .out(adder_1_out), .cin(F[2]));  // open: cout
  assign bit_extender_1_out = {{3{1'b0}}, adder_1_out[3]};  // Bit_Extender bit_extender_1
  Multiplexer #(.select(2), .width(4)) multiplexer_2 (
    .in0(A_B_out), .in1(AorB_out), .in2(adder_1_out), .in3(bit_extender_1_out), .out(out_4), .sel(F[1:0]));  // open: en
endmodule
