// Logisim project Christmas-Tree.circ as structural Verilog: 1 circuit, main circuit main
module main (
  output out_1
);

  wire clock_1_out, not_1_out, not_2_out;

  Clock clock_1 (.out(clock_1_out));
  not not_1 (not_1_out, out_1);
  D_Flip_Flop d_ff_1 (.clk(clock_1_out), .D(not_1_out), .Q(out_1));  // open: Qn, preset, en, reset
  not not_2 (not_2_out, out_1);
  LED led_1 (.in(out_1));
  LED led_2 (.in(not_2_out));
  LED led_3 (.in(not_2_out));
  LED led_4 (.in(out_1));
  LED led_5 (.in(not_2_out));
  LED led_6 (.in(out_1));
  LED led_7 (.in(out_1));
  LED led_8 (.in(not_2_out));
  LED led_9 (.in(out_1));
  LED led_10 (.in(out_1));
  LED led_11 (.in(out_1));
  LED led_12 (.in(out_1));
  LED led_13 (.in(out_1));
  LED led_14 (.in(not_2_out));
  LED led_15 (.in(out_1));
  LED led_16 (.in(not_2_out));
  LED led_17 (.in(not_2_out));
  LED led_18 (.in(out_1));
  LED led_19 (.in(out_1));
  LED led_20 (.in(out_1));
  LED led_21 (.in(out_1));
  LED led_22 (.in(1'b1));
  LED led_23 (.in(1'b1));
  LED led_24 (.in(1'b1));
  LED led_25 (.in(1'b1));
  LED led_26 (.in(1'b1));
  LED led_27 (.in(out_1));
  LED led_28 (.in(out_1));
  LED led_29 (.in(out_1));
endmodule
