// Logisim project Memory.circ as structural Verilog: 1 circuit, main circuit main
module main (
  input  in_1,
  input  in_2,
  input  [7:0] in_3,
  output [7:0] out_4
);

  wire clock_1_out, not_1_out;
  wire [7:0] counter_1_q;

  Clock clock_1 (.out(clock_1_out));
  Counter counter_1 (.Q(counter_1_q), .clk(clock_1_out), .clr(in_1));  // open: load, D, count, carry
  // Probe on out_4
  RAM ram_1 (.addr(counter_1_q), .data(out_4), .clk(clock_1_out), .ld(in_2));  // open: sel, clr
  assign out_4 = not_1_out ? in_3 : 8'bz;  // Controlled_Buffer controlled_buffer_1
  not not_1 (not_1_out, in_2);

  // Notes on the sheet:
  //   0 --> 쓰기 / 1 --> 읽기
  //   RAM: Random Access Memory
  //   쓰기에 사용하는 입력
  //   읽기에 사용하는 출력
endmodule
