// Logisim project Traffic_Controller_Design.circ as structural Verilog: 1 circuit, main circuit main
module main (
  input  Ta,
  input  Tb,
  input  Reset,
  output La1,
  output La0,
  output Lb1,
  output Lb0
);

  wire and_1_out, and_2_out, and_5_out, and_6_out, and_7_out, and_8_out, and_9_out, and_10_out, clock_1_out,
       not_1_out, not_2_out, not_3_out, not_4_out, not_5_out, not_7_out, not_8_out, not_9_out, not_10_out,
       not_11_out, not_12_out, not_13_out, not_14_out, or_1_out, S0_q, xor_1_out;

  not not_1 (not_1_out, Ta);
  not not_2 (not_2_out, S0_q);
  not not_3 (not_3_out, La1);
  not not_4 (not_4_out, Tb);
  not not_5 (not_5_out, S0_q);
  Clock clock_1 (.out(clock_1_out));
  and and_1 (and_1_out, not_1_out, not_2_out, not_3_out);
  and and_2 (and_2_out, not_4_out, La1, not_5_out);
  xor xor_1 (xor_1_out, La1, S0_q);
  or or_1 (or_1_out, and_1_out, and_2_out);
  D_Flip_Flop S1 (.clk(clock_1_out), .D(xor_1_out), .Q(La1), .reset(Reset));  // open: Qn, preset, en
  D_Flip_Flop S0 (.clk(clock_1_out), .D(or_1_out), .Q(S0_q), .reset(Reset));  // open: Qn, preset, en
  not not_6 (Lb1, La1);
  and and_3 (La0, Lb1, S0_q);
  and and_4 (Lb0, S0_q, La1);
  not not_7 (not_7_out, La1);
  not not_8 (not_8_out, La0);
  not not_9 (not_9_out, La1);
  not not_10 (not_10_out, La0);
  not not_11 (not_11_out, Lb1);
  not not_12 (not_12_out, Lb0);
  not not_13 (not_13_out, Lb1);
  not not_14 (not_14_out, Lb0);
  and and_5 (and_5_out, not_7_out, not_8_out);
  and and_6 (and_6_out, not_9_out, La0);
  and and_7 (and_7_out, La1, not_10_out);
  and and_8 (and_8_out, not_11_out, not_12_out);
  and and_9 (and_9_out, not_13_out, Lb0);
  and and_10 (and_10_out, Lb1, not_14_out);
  LED led_1 (.in(and_5_out));
  LED led_2 (.in(and_6_out));
  LED led_3 (.in(and_7_out));
  LED led_4 (.in(and_8_out));
  LED led_5 (.in(and_9_out));
  LED led_6 (.in(and_10_out));
endmodule
