// Logisim project decoder-7-seg-74HC49.circ as structural Verilog: 1 circuit, main circuit main
module main (
  input  A,
  input  B,
  input  C,
  input  D,
  input  BLANKING,
  output a_2,
  output b_2,
  output c_2,
  output d_2,
  output e,
  output f,
  output g
);

  wire and_1_out, and_2_out, and_3_out, and_4_out, and_5_out, and_6_out, and_7_out, and_8_out, and_9_out,
       and_10_out, and_11_out, and_12_out, and_13_out, and_14_out, and_15_out, and_16_out, and_17_out,
       buffer_1_out, buffer_2_out, nand_1_out, nand_2_out, nand_3_out, nand_4_out, not_1_out, not_2_out,
       not_3_out, not_4_out;

  not not_1 (not_1_out, A);
  not not_2 (not_2_out, B);
  not not_3 (not_3_out, C);
  not not_4 (not_4_out, D);
  buf buffer_1 (buffer_1_out, BLANKING);
  nand nand_1 (nand_1_out, not_1_out, buffer_1_out);
  nand nand_2 (nand_2_out, not_2_out, buffer_1_out);
  nand nand_3 (nand_3_out, not_3_out, buffer_1_out);
  nand nand_4 (nand_4_out, not_4_out, buffer_1_out);
  and and_1 (and_1_out, nand_2_out, nand_4_out);
  and and_2 (and_2_out, not_1_out, nand_3_out);
  and and_3 (and_3_out, nand_1_out, not_2_out, not_3_out, not_4_out);
  and and_4 (and_4_out, nand_2_out, nand_4_out);
  and and_5 (and_5_out, nand_1_out, not_2_out, nand_3_out);
  and and_6 (and_6_out, not_1_out, nand_2_out, nand_3_out);
  and and_7 (and_7_out, nand_3_out, nand_4_out);
  and and_8 (and_8_out, not_1_out, nand_2_out, not_3_out);
  and and_9 (and_9_out, nand_1_out, not_2_out, not_3_out);
  and and_10 (and_10_out, not_1_out, not_2_out, nand_3_out);
  and and_11 (and_11_out, nand_1_out, nand_2_out, nand_3_out);
  buf buffer_2 (buffer_2_out, nand_1_out);
  and and_12 (and_12_out, not_2_out, nand_3_out);
  and and_13 (and_13_out, nand_1_out, nand_2_out);
  and and_14 (and_14_out, nand_2_out, not_3_out);
  and and_15 (and_15_out, nand_1_out, not_3_out, not_4_out);
  and and_16 (and_16_out, nand_1_out, nand_2_out, nand_3_out);
  and and_17 (and_17_out, not_2_out, not_3_out, not_4_out);
  nor nor_1 (a_2, and_1_out, and_2_out, and_3_out);
  nor nor_2 (b_2, and_4_out, and_5_out, and_6_out);
  nor nor_3 (c_2, and_7_out, and_8_out);
  nor nor_4 (d_2, and_9_out, and_10_out, and_11_out);
  nor nor_5 (e, buffer_2_out, and_12_out);
  nor nor_6 (f, and_13_out, and_14_out, and_15_out);
  nor nor_7 (g, and_16_out, and_17_out);
  _7_Segment_Display u_7_segment_display_1 (.g(g), .f(f), .a(a_2), .b(b_2), .e(e), .d(d_2), .c(c_2));  // open: dp

  // Notes on the sheet:
  //   lsb
  //   msb
  //   (Logic 0 Blanks the display)
  //   BCD to 7-Segment Decoder Simulation
  //   (Based on 74HC49)
  //   www.learnabout-electronics.org
endmodule
