// Logisim project flipflop.circ as structural Verilog: 3 circuits, main circuit main
module main (
  input  CLK,
  input  in_2,
  output out_3
);

  wire dlatch_1_out_3, not_1_out;

  not not_1 (not_1_out, CLK);
  DLatch dlatch_1 (.CLK(in_2), .in_2(not_1_out), .out_3(dlatch_1_out_3));
  DLatch dlatch_2 (.CLK(dlatch_1_out_3), .in_2(CLK), .out_3(out_3));
endmodule

module SRLatch (
  input  Reset,
  input  Set,
  output Qout,
  output Qbout
);

  nor nor_1 (Qout, Reset, Qbout);
  nor nor_2 (Qbout, Qout, Set);
endmodule

module DLatch (
  input  CLK,
  input  in_2,
  output out_3
);

  wire and_1_out, and_2_out, not_1_out;

  not not_1 (not_1_out, in_2);
  and and_1 (and_1_out, CLK, not_1_out);
  and and_2 (and_2_out, CLK, in_2);
  SRLatch srlatch_1 (.Reset(and_1_out), .Set(and_2_out), .Qout(out_3));  // open: Qbout
endmodule
