// Logisim project multiplier.circ as structural Verilog: 1 circuit, main circuit main
module main (
  input  [3:0] a,
  input  [2:0] in_2,
  input  [3:0] b,
  input  [7:0] in_4,
  input  [2:0] in_5,
  input  [2:0] in_6,
  output out_7,
  output [7:0] out_8
);

  wire clock_1_out, comparator_1_gt, comparator_2_eq, nor_1_out;
  wire [2:0] counter_1_q;
  wire [7:0] adder_1_out, ar_q, bit_extender_1_out, multiplexer_1_out, multiplexer_2_out, shifter_1_out;

  Clock clock_1 (.out(clock_1_out));
  // Probe on a
  // Probe on b
  Counter #(.width(3), .max('h7)) counter_1 (
    .Q(counter_1_q), .clk(clock_1_out), .clr(comparator_2_eq));  // open: load, D, count, carry
  assign bit_extender_1_out = {{4{1'b0}}, a};  // Bit_Extender bit_extender_1
  Shift_Register #(.length(4)) shift_register_1 (
    .in(1'b0), .clk(clock_1_out), .out(out_7), .load(nor_1_out), .d0(b[3]), .d1(b[2]), .d2(b[1]), .d3(b[0]));  // open: shift, clr, q0, q1, q2, q3
  Multiplexer #(.width(8)) multiplexer_1 (
    .in0(shifter_1_out), .in1(bit_extender_1_out), .out(multiplexer_1_out), .sel(nor_1_out));  // open: en
  Comparator #(.width(3), .mode("unsigned")) comparator_1 (
    .a(counter_1_q), .b(in_5), .gt(comparator_1_gt));  // open: eq, lt
  Comparator #(.width(3), .mode("unsigned")) comparator_2 (
    .a(counter_1_q), .b(in_6), .eq(comparator_2_eq));  // open: gt, lt
  Register ar (.D(multiplexer_1_out), .Q(ar_q), .clk(clock_1_out));  // open: en, clr
  nor nor_1 (nor_1_out, counter_1_q[0], counter_1_q[1], counter_1_q[2]);
  Multiplexer #(.width(8)) multiplexer_2 (.in0(in_4), .in1(ar_q), .out(multiplexer_2_out), .sel(out_7));  // open: en
  Shifter shifter_1 (.in(ar_q), .\dist (in_2), .out(shifter_1_out));
  Adder adder_1 (.a(multiplexer_2_out), .b(out_8), .out(adder_1_out));  // open: cin, cout
  Register ar_2 (.D(adder_1_out), .Q(out_8), .clk(clock_1_out), .clr(nor_1_out));  // open: en
  LED led_1 (.in(comparator_1_gt));
  // Probe on out_8
endmodule
