// Logisim project scissor-rock-paper.circ as structural Verilog: 1 circuit, main circuit main
module main (
  input  [1:0] Scissor,
  input  [1:0] Rock,
  input  in_3,
  input  [1:0] Paper
);

  wire clock_1_out, comparator_1_eq, comparator_2_eq, comparator_3_eq, controlled_buffer_1_out, or_1_out,
       or_2_out;
  wire [1:0] random_1_out;

  Clock clock_1 (.out(clock_1_out));
  assign controlled_buffer_1_out = in_3 ? clock_1_out : 1'bz;  // Controlled_Buffer controlled_buffer_1
  Random #(.width(2)) random_1 (.clk(controlled_buffer_1_out), .out(random_1_out));  // open: next, clr
  Comparator #(.width(2)) comparator_1 (.a(Scissor), .b(random_1_out), .eq(comparator_1_eq));  // open: gt, lt
  Comparator #(.width(2)) comparator_2 (.a(Rock), .b(random_1_out), .eq(comparator_2_eq));  // open: gt, lt
  Comparator #(.width(2)) comparator_3 (.a(Paper), .b(random_1_out), .eq(comparator_3_eq));  // open: gt, lt
  or or_1 (or_1_out, comparator_1_eq, comparator_3_eq);
  or or_2 (or_2_out, comparator_1_eq, comparator_2_eq, comparator_3_eq);
  LED led_1 (.in(comparator_3_eq));
  LED led_2 (.in(or_1_out));
  LED led_3 (.in(or_1_out));
  LED led_4 (.in(or_1_out));
  LED led_5 (.in(or_1_out));
  LED led_6 (.in(or_2_out));
  LED led_7 (.in(or_2_out));
  LED led_8 (.in(or_2_out));
  LED led_9 (.in(comparator_3_eq));
  LED led_10 (.in(or_2_out));
  LED led_11 (.in(or_1_out));
  LED led_12 (.in(comparator_3_eq));
  LED led_13 (.in(or_1_out));
  LED led_14 (.in(comparator_3_eq));
  LED led_15 (.in(or_1_out));
  LED led_16 (.in(comparator_3_eq));
  LED led_17 (.in(or_1_out));
  LED led_18 (.in(comparator_3_eq));
  LED led_19 (.in(or_2_out));
  LED led_20 (.in(or_2_out));
  LED led_21 (.in(or_2_out));
  LED led_22 (.in(or_2_out));
  LED led_23 (.in(or_2_out));
  LED led_24 (.in(or_2_out));
  LED led_25 (.in(comparator_3_eq));
  LED led_26 (.in(comparator_3_eq));
  LED led_27 (.in(comparator_3_eq));
  LED led_28 (.in(or_2_out));
  LED led_29 (.in(or_2_out));
  LED led_30 (.in(or_2_out));
  LED led_31 (.in(or_2_out));
endmodule
