// Logisim project 신호등제어기.circ as structural Verilog: 1 circuit, main circuit main
module main (
  input  Ta,
  input  Tb,
  output out_3,
  output out_4,
  output out_5,
  output out_6
);

  wire and_1_out, and_2_out, clock_1_out, not_1_out, not_2_out, not_3_out, not_4_out, or_1_out, S0_q,
       xor_1_out;

  not not_1 (not_1_out, Tb);
  not not_2 (not_2_out, Ta);
  not not_3 (not_3_out, out_3);
  not not_4 (not_4_out, S0_q);
  Clock clock_1 (.out(clock_1_out));
  xor xor_1 (xor_1_out, out_3, S0_q);
  and and_1 (and_1_out, not_2_out, not_4_out, not_3_out);
  and and_2 (and_2_out, not_4_out, out_3, not_1_out);
  or or_1 (or_1_out, and_1_out, and_2_out);
  D_Flip_Flop S1 (.clk(clock_1_out), .D(xor_1_out), .Q(out_3));  // open: Qn, preset, en, reset
  D_Flip_Flop S0 (.clk(clock_1_out), .D(or_1_out), .Q(S0_q));  // open: Qn, preset, en, reset
  not not_5 (out_5, out_3);
  and and_3 (out_4, out_5, S0_q);
  and and_4 (out_6, out_3, S0_q);
endmodule
